// Logisim project Aniol64keyboard.circ as structural Verilog: 1 circuit, main circuit main
module main (
  input  in_1,
  input  IEI,
  input  in_3,
  output IEO,
  output INT
);

  wire and_1_out, CLK, demultiplexer_1_out0, demultiplexer_1_out3, j_k_ff_1_q, j_k_ff_1_qn,
       multiplexer_1_out, or_1_out, switch_1_p1, switch_1_p3, switch_1_p7, switch_1_p8;
  wire [6:0] counter_1_q;

  Clock clock_1 (.out(CLK));
  Counter #(.max('h7f), .width(7)) counter_1 (
    .clr(in_1), .clk(or_1_out), .Q(counter_1_q));  // open: load, up, count, D, carry
  or or_1 (or_1_out, CLK, and_1_out);
  Register #(.width(7)) register_1 (.D(counter_1_q), .clk(and_1_out));  // open: en, Q, clr
  LED led_1 (.in(multiplexer_1_out));
  Multiplexer #(.enable("false"), .select(3)) multiplexer_1 (
    .in2(switch_1_p7), .out(multiplexer_1_out), .sel(counter_1_q[6:4]));  // open: in0, in1, in3, in4, in5, in6, in7
  J_K_Flip_Flop j_k_ff_1 (
    .J(multiplexer_1_out), .K(in_3), .clk(CLK), .Q(j_k_ff_1_q), .Qn(j_k_ff_1_qn));  // open: preset, reset
  and and_1 (and_1_out, j_k_ff_1_q, IEI);
  Demultiplexer #(.enable("false"), .select(4)) demultiplexer_1 (
    .out0(demultiplexer_1_out0), .out3(demultiplexer_1_out3), .in(1'b1), .sel(counter_1_q[3:0]));  // open: out1, out2, out4, out5, out6, out7, out8, out9, out10, out11, out12, out13, out14, out15
  // Switch switch_1: pin names not known; wires that end beside it: switch_1_p1, switch_1_p1, switch_1_p3, demultiplexer_1_out0, switch_1_p3, demultiplexer_1_out3, switch_1_p7, switch_1_p8, switch_1_p8
  not not_1 (INT, and_1_out);
  and and_2 (IEO, IEI, j_k_ff_1_qn);
endmodule
